# Fritzing sketch SmartDrawings (saved by Fritzing 0.7.0b)
breadboards: 1

parts:
  R1 = Resistor [tolerance=±5% resistance=1M package=THT]
  Arduino_Ethernet_Shield1 = Arduino Ethernet Shield
  R2 = Resistor [tolerance=±5% resistance=1M package=THT]
  R3 = Resistor [tolerance=±5% resistance=1M package=THT]
  R4 = Resistor [tolerance=±5% resistance=1M package=THT]
  R6 = Resistor [tolerance=±5% resistance=1M package=THT]
  R7 = Resistor [tolerance=±5% resistance=220 package=THT]
  R8 = Resistor [tolerance=±5% resistance=1M package=THT]
  LED1 = LED - 5mm [color="Green (570nm)" package="5 mm [THT]"]

nets:
  N1: R1.Pin_0, R2.Pin_0, R3.Pin_0, R4.Pin_0, R6.Pin_0, R8.Pin_0
  N2: R1.Pin_1, Arduino_Ethernet_Shield1.D7
  N3: Arduino_Ethernet_Shield1.D9, R7.Pin_1
  N4: Arduino_Ethernet_Shield1.D6, R2.Pin_1
  N5: Arduino_Ethernet_Shield1.D5, R3.Pin_1
  N6: Arduino_Ethernet_Shield1.SS, R4.Pin_1
  N7: Arduino_Ethernet_Shield1.D3, R8.Pin_1
  N8: Arduino_Ethernet_Shield1.D2, R6.Pin_1
  N9: Arduino_Ethernet_Shield1.GND, LED1.cathode
  N10: R7.Pin_0, LED1.anode

notes:
  Make your draws here!
